# Fritzing sketch LDR&LED (saved by Fritzing 0.9.3b)
breadboards: 1

parts:
  R1 = Photocell (LDR) [package=THT]
  LED1 = LED - 5mm [color="Red (633nm)" package="5 mm [THT]"]
  Part1 = Arduino Uno (Rev3) - ICSP
  R2 = Resistor [tolerance=±5% resistance=220 package="0402 [SMD]"]

nets:
  N1: R1.pin_0, Part1.GND, R2.Pin_1
  N2: R1.pin_1, LED1.cathode
  N3: LED1.anode, Part1.ICSP_MOSI, Part1.D11_PWM/MOSI

// code stored in the sketch: LDR&LED.ino
const int lamp = 7;
boolean x = true;
void setup() {
  Serial.begin(9600);
  pinMode(lamp , OUTPUT);

}

void loop() {
  int c = analogRead(A0);
  delay(500);
if ( c<300 && x == true){
  digitalWrite(7,HIGH);
   x = false;
   delay(1000);

}
else if ( c <300 && x == false){
x = true;
digitalWrite(7,LOW);
delay(1000);
}
}

// code stored in the sketch: toggle_ldr.ino
const int lamp = 7;
boolean x = true;
void setup() {
  Serial.begin(9600);
  pinMode(lamp , OUTPUT);

}

void loop() {
  int c = analogRead(A0);
  delay(500);
if ( c<300 && x == true){
  digitalWrite(7,HIGH);
   x = false;
   delay(1000);

}
else if ( c <300 && x == false){
x = true;
digitalWrite(7,LOW);
delay(1000);
}
}
